# Fritzing sketch servotester (saved by Fritzing 0.9.3b)

parts:
  part = Adafruit RGB LCD Pi Plate
  J1 = Basic Servo
  Bauteil1 = Arduino Pro Mini v13
  5V_Regulator = Voltage Regulator - 3.3V [package="TO220 [THT]"]  # not connected
  5V_Regulator_2 = Voltage Regulator - 3.3V [package="TO220 [THT]"]
  J2 = Power Jack [package=power_jack_combo]

nets:
  N1: part.+5V, Bauteil1.RAW
  N2: part.SDA, Bauteil1.D2
  N3: part.SCL, Bauteil1.D3_PWM
  GND: part.GND, Bauteil1.GND
  GND_2: J1.gnd, 5V_Regulator_2.GND, J2.GNDBREAK
  N4: J1.vcc, 5V_Regulator_2.output_voltage
  N5: J1.pulse, Bauteil1.D7
  N6: 5V_Regulator_2.input_voltage, J2.PWR

custom parts:
  Adafruit RGB LCD Pi Plate: This new Adafruit Pi Plate makes it easy to use an RGB 16x2 Character LCD. We really like the RGB Character LCDs we stock in the shop. (For RGB we have RGB negative and RGB positive.) Unfortunately, these LCDs do require quite a few digital pins, 6 to control the LCD and then another 3 to control the RGB backlight for a total of 9 pins. That's nearly all the GPIO available on a Pi! With this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
